# Fritzing sketch NRF24L01_Connection (saved by Fritzing 0.9.3b)

parts:
  Part1 = Arduino Uno (Rev3)
  Part3 = NRF24L01+ Breakout Board
  Part4 = Arduino Joystick Shield  # not connected
  Part5 = NRF24L01+ Breakout Board  # not connected

nets:
  N1: Part1.D8, Part3.CS
  N2: Part1.D11_PWM/MOSI, Part3.MOSI
  N3: Part1.D12/MISO, Part3.MISO
  N4: Part1.D13/SCK, Part3.SCK
  N5: Part1.D7, Part3.CE
  3V3: Part1.3V3, Part3.VCC
  GND: Part1.GND, Part3.GND

notes:
  1- GND
  2- 3.3v
  3- pin 7
  4- pin 8
  5- pin 13
  6- pin 11
  7- pin 12
  Arduino NANO/UNO
